# Fritzing sketch Layout (saved by Fritzing 0.9.3b)
circuit board: 15cm x 11.2cm
breadboards: 4

parts:
  7_Segment30 = 7 Segment Display
  7_Segment31 = 7 Segment Display
  7_Segment32 = 7 Segment Display
  7_Segment33 = 7 Segment Display
  7_Segment34 = 7 Segment Display
  7_Segment35 = 7 Segment Display
  7_Segment36 = 7 Segment Display
  7_Segment37 = 7 Segment Display
  7_Segment38 = 7 Segment Display
  7_Segment39 = 7 Segment Display
  7_Segment40 = 7 Segment Display
  7_Segment41 = 7 Segment Display
  7_Segment42 = 7 Segment Display
  7_Segment43 = 7 Segment Display
  7_Segment44 = 7 Segment Display
  7_Segment45 = 7 Segment Display
  7_Segment46 = 7 Segment Display
  MAX_7224 = MAX 7219 [package="DIP (Dual Inline) [THT]"]
  MAX_7225 = MAX 7219 [package="DIP (Dual Inline) [THT]"]
  MAX7219CNG = MAX 7219 [package="DIP (Dual Inline) [THT]"]
  ISET6 = Resistor [tolerance=±5% resistance=220 package=THT]
  ISET7 = Resistor [tolerance=±5% resistance=220 package=THT]
  10k = Resistor [tolerance=±5% resistance=220 package=THT]
  S4 = Tactile Switch Buttons - 12mm Square [package=tactile-pth-12mm]
  S5 = Tactile Switch Buttons - 12mm Square [package=tactile-pth-12mm]
  DS1307_RTC = Real Time Clock Module - DS1307 RTC Breakout Board
  Bauteil5 = Arduino Nano (Rev3.0)
  10NF = Tantalum Capacitor [capacitance=1μF package="200 mil [THT, tantalum]"]
  100NF = Tantalum Capacitor [capacitance=1μF package="200 mil [THT, tantalum]"]
  S6 = Tactile Switch Buttons - 12mm Square [package=tactile-pth-12mm]

nets:
  N1: 7_Segment30.Segment_E, 7_Segment33.Segment_E, 7_Segment36.Segment_E, 7_Segment39.Segment_E, 7_Segment44.Segment_E, MAX_7224.SEG_E
  N2: 7_Segment30.Segment_D, 7_Segment33.Segment_D, 7_Segment36.Segment_D, 7_Segment39.Segment_D, 7_Segment44.Segment_D, MAX_7224.SEG_D
  N3: 7_Segment30.common_cathode, MAX_7224.DIG_0
  N4: 7_Segment30.Segment_C, 7_Segment33.Segment_C, 7_Segment36.Segment_C, 7_Segment39.Segment_C, 7_Segment44.Segment_C, MAX_7224.SEG_C
  N5: 7_Segment30.Segment_DP, 7_Segment33.Segment_DP, 7_Segment36.Segment_DP, 7_Segment39.Segment_DP, 7_Segment44.Segment_DP, MAX_7224.SEG_DP
  N6: 7_Segment30.Segment_B, 7_Segment33.Segment_B, 7_Segment36.Segment_B, 7_Segment39.Segment_B, 7_Segment44.Segment_B, MAX_7224.SEG_B
  N7: 7_Segment30.Segment_A, 7_Segment33.Segment_A, 7_Segment36.Segment_A, 7_Segment39.Segment_A, 7_Segment44.Segment_A, MAX_7224.SEG_A
  N8: 7_Segment30.Segment_F, 7_Segment33.Segment_F, 7_Segment36.Segment_F, 7_Segment39.Segment_F, 7_Segment44.Segment_F, MAX_7224.SEG_F
  N9: 7_Segment30.Segment_G, 7_Segment33.Segment_G, 7_Segment36.Segment_G, 7_Segment39.Segment_G, 7_Segment44.Segment_G, MAX_7224.SEG_G
  N10: 7_Segment31.Segment_E, 7_Segment34.Segment_E, 7_Segment37.Segment_E, 7_Segment40.Segment_E, 7_Segment42.Segment_E, 7_Segment45.Segment_E, MAX_7225.SEG_E
  N11: 7_Segment31.Segment_D, 7_Segment34.Segment_D, 7_Segment37.Segment_D, 7_Segment40.Segment_D, 7_Segment42.Segment_D, 7_Segment45.Segment_D, MAX_7225.SEG_D
  N12: 7_Segment31.common_cathode, MAX_7225.DIG_0
  N13: 7_Segment31.Segment_C, 7_Segment34.Segment_C, 7_Segment37.Segment_C, 7_Segment40.Segment_C, 7_Segment42.Segment_C, 7_Segment45.Segment_C, MAX_7225.SEG_C
  N14: 7_Segment31.Segment_DP, 7_Segment34.Segment_DP, 7_Segment37.Segment_DP, 7_Segment40.Segment_DP, 7_Segment42.Segment_DP, 7_Segment45.Segment_DP, MAX_7225.SEG_DP
  N15: 7_Segment31.Segment_B, 7_Segment34.Segment_B, 7_Segment37.Segment_B, 7_Segment40.Segment_B, 7_Segment42.Segment_B, 7_Segment45.Segment_B, MAX_7225.SEG_B
  N16: 7_Segment31.Segment_A, 7_Segment34.Segment_A, 7_Segment37.Segment_A, 7_Segment40.Segment_A, 7_Segment42.Segment_A, 7_Segment45.Segment_A, MAX_7225.SEG_A
  N17: 7_Segment31.Segment_F, 7_Segment34.Segment_F, 7_Segment37.Segment_F, 7_Segment40.Segment_F, 7_Segment42.Segment_F, 7_Segment45.Segment_F, MAX_7225.SEG_F
  N18: 7_Segment31.Segment_G, 7_Segment34.Segment_G, 7_Segment37.Segment_G, 7_Segment40.Segment_G, 7_Segment42.Segment_G, 7_Segment45.Segment_G, MAX_7225.SEG_G
  N19: 7_Segment32.Segment_E, 7_Segment35.Segment_E, 7_Segment38.Segment_E, 7_Segment41.Segment_E, 7_Segment43.Segment_E, 7_Segment46.Segment_E, MAX7219CNG.SEG_E
  N20: 7_Segment32.Segment_D, 7_Segment35.Segment_D, 7_Segment38.Segment_D, 7_Segment41.Segment_D, 7_Segment43.Segment_D, 7_Segment46.Segment_D, MAX7219CNG.SEG_D
  N21: 7_Segment32.common_cathode, MAX7219CNG.DIG_0
  N22: 7_Segment32.Segment_C, 7_Segment35.Segment_C, 7_Segment38.Segment_C, 7_Segment41.Segment_C, 7_Segment43.Segment_C, 7_Segment46.Segment_C, MAX7219CNG.SEG_C
  N23: 7_Segment32.Segment_DP, 7_Segment35.Segment_DP, 7_Segment38.Segment_DP, 7_Segment41.Segment_DP, 7_Segment43.Segment_DP, 7_Segment46.Segment_DP, MAX7219CNG.SEG_DP
  N24: 7_Segment32.Segment_B, 7_Segment35.Segment_B, 7_Segment38.Segment_B, 7_Segment41.Segment_B, 7_Segment43.Segment_B, 7_Segment46.Segment_B, MAX7219CNG.SEG_B
  N25: 7_Segment32.Segment_A, 7_Segment35.Segment_A, 7_Segment38.Segment_A, 7_Segment41.Segment_A, 7_Segment43.Segment_A, 7_Segment46.Segment_A, MAX7219CNG.SEG_A
  N26: 7_Segment32.Segment_F, 7_Segment35.Segment_F, 7_Segment38.Segment_F, 7_Segment41.Segment_F, 7_Segment43.Segment_F, 7_Segment46.Segment_F, MAX7219CNG.SEG_F
  N27: 7_Segment32.Segment_G, 7_Segment35.Segment_G, 7_Segment38.Segment_G, 7_Segment41.Segment_G, 7_Segment43.Segment_G, 7_Segment46.Segment_G, MAX7219CNG.SEG_G
  N28: 7_Segment33.common_cathode, MAX_7224.DIG_1
  N29: 7_Segment34.common_cathode, MAX_7225.DIG_1
  N30: 7_Segment35.common_cathode, MAX7219CNG.DIG_1
  N31: 7_Segment36.common_cathode, MAX_7224.DIG_2
  N32: 7_Segment37.common_cathode, MAX_7225.DIG_2
  N33: 7_Segment38.common_cathode, MAX7219CNG.DIG_2
  N34: 7_Segment39.common_cathode, MAX_7224.DIG_3
  N35: 7_Segment40.common_cathode, MAX_7225.DIG_3
  N36: 7_Segment41.common_cathode, MAX7219CNG.DIG_3
  N37: 7_Segment42.common_cathode, MAX_7225.DIG_5
  N38: 7_Segment43.common_cathode, MAX7219CNG.DIG_5
  N39: 7_Segment44.common_cathode, MAX_7224.DIG_4
  N40: 7_Segment45.common_cathode, MAX_7225.DIG_4
  N41: 7_Segment46.common_cathode, MAX7219CNG.DIG_4
  N42: MAX_7224.DIN, MAX_7225.DOUT
  GND: MAX_7224.GND, MAX_7225.GND, MAX7219CNG.GND, S4.2, S4.4, S5.2, S5.4, DS1307_RTC.GND, Bauteil5.GND, 10NF.-, 100NF.-, S6.2, S6.4
  N43: MAX_7224.LOAD_(CS), MAX_7225.LOAD_(CS), MAX7219CNG.LOAD_(CS), Bauteil5.D10
  N44: MAX_7224.CLK, MAX_7225.CLK, MAX7219CNG.CLK, Bauteil5.D11/MOSI
  N45: MAX_7224.ISET, ISET6.Pin_1
  5V: MAX_7224.V+, MAX_7225.V+, MAX7219CNG.V+, ISET6.Pin_0, ISET7.Pin_0, 10k.Pin_0, DS1307_RTC.5V, Bauteil5.5V, 10NF.+, 100NF.+
  N46: MAX_7225.DIN, MAX7219CNG.DOUT
  N47: MAX_7225.ISET, ISET7.Pin_1
  N48: MAX7219CNG.DIN, Bauteil5.D12/MISO
  N49: MAX7219CNG.ISET, 10k.Pin_1
  N50: S4.1, S4.3, Bauteil5.D7
  N51: S5.1, S5.3, Bauteil5.D6
  N52: DS1307_RTC.SCL, Bauteil5.A5
  N53: DS1307_RTC.SDA, Bauteil5.A4
  N54: Bauteil5.D5, S6.1, S6.3

notes:
  RUUM42.CH
  CUSTOMER ID

custom parts:
  MAX 7219: A led matrix driver on a 300 mil dual inline package (DIP) footprint.
  Tactile Switch Buttons - 12mm Square: Medium-sized clicky momentary switches are standard input "buttons" on electronic projects. These work best in a PCB but can be used on a solderless breadboard as shown in this tutorial. The pins are normally open (disconnected) and when the button is pressed they are momentarily closed. They come in a pack of 10, they're pretty handy so you'll want to keep them around. You can find an EAGLE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
